# Fritzing sketch bluetoothCar (saved by Fritzing 0.9.3b)
breadboards: 1

parts:
  부품1 = Arduino Uno (Rev3)
  M1 = DC Motor  # not connected
  부품2 = Bluetooth HC-05 Macho  # not connected
  M2 = DC Motor  # not connected
  BAT1 = Battery Holders [package=battery-aa]
  부품3 = Arduino Modkit Shield

nets:
  N1: 부품1.D9_PWM, 부품3.DB1
  N2: 부품1.D10_PWM/SS, 부품3.D10
  N3: 부품1.D4, 부품3.DB2
  N4: 부품1.D5_PWM, 부품3.DB3
  N5: 부품1.D6_PWM, 부품3.D8
  N6: 부품1.D7, 부품3.D9
  N7: 부품1.5V, BAT1.-
  N8: 부품1.GND, BAT1.+

notes:
  ENB IN4 IN3 IN2 IN1 ENA
  하단의 핀 6개를 위의 순서로 가정하겠습니다.
  * L298N모듈이 없어서 부득이 유사한 모듈로 대채합니다.
  HC-06모듈로 연결하시기 바랍니다.
  OUT1
  OUT2
  OUT3
  OUT4
