# Fritzing sketch CheckDoor (saved by Fritzing 0.9.3b)
breadboards: 1

parts:
  R1 = PHOTOCELL [package=photocell-kit]
  LED1 = RGB LED (com. anode, rbg) [package="5 mm [THT]"]
  hc-sr1 = hc-sr04
  Part1 = Arduino Nano (Rev3.0) (ICSP)
  R2 = Resistor [tolerance=±5% resistance=10k package="0805 [SMD]"]

nets:
  VCC: R1.P$1, hc-sr1.VCC, Part1.5V
  N1: R1.P$2, Part1.A0, R2.Pin_0
  N2: LED1.red_cathode, Part1.D9
  N3: LED1.common_anode, Part1.D8
  GND: LED1.blue_cathode, hc-sr1.GND, Part1.GND, R2.Pin_1
  N4: hc-sr1.Trig, Part1.D2
  N5: hc-sr1.Echo, Part1.D3
