# Fritzing sketch RGB_led (saved by Fritzing 0.9.3b)
breadboards: 1

parts:
  LED1 = RGB LED (com. anode, rbg) [package="5 mm [THT]"]
  R1 = Resistor [tolerance=±5% resistance=220 package="0603 [SMD]"]
  Part1 = Arduino Nano (Rev3.0)

nets:
  N1: LED1.red_cathode, Part1.D11/MOSI
  N2: LED1.common_anode, R1.Pin_1
  N3: LED1.blue_cathode, Part1.D10
  N4: LED1.green_cathode, Part1.D8
  N5: R1.Pin_0, Part1.5V
