# Fritzing sketch circuit exam (saved by Fritzing 0.9.2b)
breadboards: 1

parts:
  부품1 = Arduino Uno (Rev3) - ICSP
  LED1 = smd LED [color="Red (633nm)" package="0603 [SMD]"]
  LED2 = smd LED [color="Red (633nm)" package="0603 [SMD]"]
  R1 = Resistor [tolerance=±5% resistance=220 package=THT]
  R2 = Resistor [tolerance=±5% resistance=220 package=THT]

nets:
  N1: 부품1.ICSP_MOSI, 부품1.D11_PWM/MOSI, R2.Pin_1
  N2: 부품1.D13/SCK, R1.Pin_1
  N3: 부품1.GND, LED1.cathode, LED2.cathode
  N4: LED1.anode, R1.Pin_0
  N5: LED2.anode, R2.Pin_0
