# Fritzing sketch circuit (saved by Fritzing 0.9.4)

parts:
  부품1 = Arduino Uno (Rev3)
  부품2 = Bluetooth HC-05 Macho
  LED1 = LEDs [package=led10mm]

nets:
  N1: 부품1.D10_PWM/SS, 부품2.TXD
  N2: 부품1.D11_PWM/MOSI, 부품2.RXD
  N3: 부품1.D13/SCK, LED1.A
  GND: 부품1.GND, 부품2.GND
  5V: 부품1.5V, 부품2.VCC
