# Fritzing sketch cds_and_led (saved by Fritzing 0.9.3b)
breadboards: 1

parts:
  Part1 = Arduino Uno (Rev3)
  R1 = PHOTOCELL [package=photocell-kit]
  R2 = Resistor [tolerance=±5% resistance=10k package="0603 [SMD]"]
  LED1 = LED - 5mm [color="Red (633nm)" package="5 mm [THT]"]

nets:
  N1: Part1.A0, R1.P$2, R2.Pin_0
  N2: Part1.GND, R2.Pin_1, LED1.cathode
  N3: Part1.D3_PWM, LED1.anode
  N4: Part1.5V, R1.P$1
